# Fritzing sketch schematic (saved by Fritzing 1.0.6)
breadboards: 1

parts:
  A1 = photon2
  C1 = Ceramic Capacitor [capacitance="100 nF" voltage=35V package="0603 [SMD, multilayer]"]
  C2 = Ceramic Capacitor [capacitance="100 nF" voltage=35V package="0603 [SMD, multilayer]"]
  S1 = Momentary Switch [package=ksa_sealed_tac_switch]

nets:
  N1: A1.Pin_2, A1.Pin_31, C1.1, S1.3
  N2: A1.Pin_4, A1.Pin_30, C1.0, C2.0
  N3: A1.Pin_20, S1.2
  N4: A1.Pin_26, C2.1
  N5: A1.Pin_28, A1.Pin_29

custom parts:
  photon2: The Photon 2 is a development module with a microcontroller and Wi-Fi networking.
